# Fritzing sketch LightClock (saved by Fritzing 0.9.0b)
breadboards: 1

parts:
  Part1 = Arduino Uno (Rev3)
  HOURS = Neopixel Ring 12
  24H = Neopixel 24 Ring
  R1 = Resistor [tolerance=±5% resistance=330 package=THT]
  R2 = Resistor [tolerance=±5% resistance=330 package=THT]
  R3 = Resistor [tolerance=±5% resistance=330 package=THT]
  JACK1 = 2.1mm Barrel Jack with Terminal Block
  C1 = Electrolytic Capacitor [capacitance=1mF voltage=35V package="300 mil [THT, electrolytic]"]
  ON/OFF = Waterproof Pushbutton (blue)
  PIR_OVERRIDE = Waterproof Pushbutton (blue)
  PIR_(PARALLAX) = PIR sensor
  RTC_(CHRONODOT) = DS1307 RTC Breakout

nets:
  N1: Part1.A4/SDA, RTC_(CHRONODOT).SDA
  N2: Part1.A5/SCL, RTC_(CHRONODOT).SCL
  N3: Part1.D2, PIR_OVERRIDE.no_name_yet#2
  N4: Part1.D3_PWM, PIR_(PARALLAX).SIG
  N5: Part1.D4, R2.Pin_0
  N6: Part1.D5_PWM, R3.Pin_0
  N7: Part1.D6_PWM, R1.Pin_0
  N8: Part1.D7, PIR_OVERRIDE.no_name_yet#4
  5V: Part1.5V, RTC_(CHRONODOT).5V
  GND: Part1.GND, RTC_(CHRONODOT).GND
  GND_2: HOURS.GND, 24H.GND, ON/OFF.no_name_yet#5, PIR_OVERRIDE.no_name_yet#1, PIR_OVERRIDE.no_name_yet#5, PIR_(PARALLAX).GND
  VCC: HOURS.VCC, 24H.Vcc, ON/OFF.no_name_yet#1, ON/OFF.no_name_yet#4, PIR_(PARALLAX).VDD
  N9: HOURS.IN, R1.Pin_1
  N10: 24H.IN, R2.Pin_1
  N11: JACK1.POS, C1.+, ON/OFF.no_name_yet#2
  N12: JACK1.NEG, C1.-

notes:
  NeoPixel 60 LEDs Ring

custom parts:
  Neopixel Ring 12: Neopixel Ring x12
  Waterproof Pushbutton (blue): Waterproof Illuminated Pushbutton (blue)
  DS1307 RTC Breakout: DS1307 Real-time Clock Breakout Board with Battery
